# Fritzing sketch Obstacle avoidance car fritzing (saved by Fritzing 0.9.2b)
breadboards: 1

parts:
  Part1 = Arduino Uno (Rev3) - ICSP
  S1 = H-Bridge with L298N
  Part2 = SRF05 Ultrasonic Rangefinder
  BAT1 = Battery Holders [package=lipo-1100mAh]
  M2 = DC Motor
  M1 = DC Motor

nets:
  N1: Part1.ICSP_MISO, Part1.D12/MISO, Part2.Trig
  N2: Part1.ICSP_MOSI, Part1.D11_PWM/MOSI, Part2.Echo
  N3: Part1.D8, S1.IN2
  N4: Part1.D9_PWM, S1.IN1
  N5: Part1.D10_PWM/SS, S1.ENA
  N6: Part1.D5_PWM, S1.ENB
  N7: Part1.D6_PWM, S1.IN4
  N8: Part1.D7, S1.IN3
  5V: Part1.5V, Part2.VCC
  GND: Part1.GND, Part2.GND
  N9: S1.GND, BAT1.-
  N10: S1.5V, BAT1.+
  N11: S1.M1-01, M2.pin_2
  N12: S1.M1-02, M2.pin_1
  N13: S1.M2-01, M1.pin_2
  N14: S1.M2-02, M1.pin_1

custom parts:
  H-Bridge with L298N: h-bridge
